// Logisim project BigASM #53 Diferencia de Conjuntos.circ as structural Verilog
module BOARD_BIG_ASM (
  output out_1
);

  wire button_1_out, CLK, CLR, d_ff_1_q, not_1_out, Write, Write_ASCII;
  wire [6:0] ASCII;
  wire [7:0] counter_1_q;
  wire [23:0] Dir_INPUT, Dir_MEMORY;
  wire [31:0] INPUT, MEMORY_IN, MEMORY_OUT;

  Button button_1 (.out(button_1_out));
  Clock clock_1 (.out(CLK));
  D_Flip_Flop d_ff_1 (.clk(CLK), .D(1'b1), .Q(d_ff_1_q), .reset(button_1_out));  // open: Qn, preset, en
  D_Flip_Flop d_ff_2 (.clk(CLK), .D(d_ff_1_q), .Qn(CLR), .reset(button_1_out));  // open: Q, preset, en
  BIG_ASM big_asm_1 (
    .DATA_INPUT(INPUT), .MEMORY_IN(MEMORY_OUT), .CLK(CLK), .CLR(CLR), .DIR_INPUT(Dir_INPUT),
    .MEMORY_OUT(MEMORY_IN), .DIR_MEMORY(Dir_MEMORY), .Write_OUTPUT(Write), .ASCII(ASCII),
    .Write_ASCII(Write_ASCII), .END(out_1));
  MEMORY memory_1 (.DIR(Dir_MEMORY), .DATA_IN(MEMORY_IN), .WRITE(Write), .CLK(CLK), .CLR(CLR), .DATA_OUT(MEMORY_OUT));
  INPUT input_1 (.DIR(Dir_INPUT), .CLK(CLK), .DATA_OUT(INPUT));
  Counter counter_1 (.load(1'b0), .count(not_1_out), .Q(counter_1_q), .clk(CLK), .clr(CLR));  // open: D, carry
  not not_1 (not_1_out, out_1);
  // Probe on counter_1_q
  TTY #(.rows(32), .cols(60)) tty_1 (.data(ASCII), .clk(CLK), .we(Write_ASCII), .clr(CLR));

  // Other names for the same wires on the sheet: END = out_1

  // Notes on the sheet:
  //   COUNTER
  //   BOARD
endmodule

module INPUT (
  input  [23:0] DIR,
  input  CLK,
  output [31:0] DATA_OUT
);

  RAM #(.addrWidth(24), .dataWidth(32)) ram_1 (.addr(DIR), .data(DATA_OUT), .clk(CLK), .ld(1'b1));  // open: sel, clr
endmodule

module MEMORY (
  input  [23:0] DIR,
  input  [31:0] DATA_IN,
  input  WRITE,
  input  CLK,
  input  CLR,
  output [31:0] DATA_OUT
);

  wire not_1_out;

  not not_1 (not_1_out, WRITE);
  RAM #(.addrWidth(24), .dataWidth(32), .bus("separate")) ram_1 (
    .addr(DIR), .din(DATA_IN), .data(DATA_OUT), .clk(CLK), .ld(not_1_out), .clr(CLR));  // open: str, sel
endmodule

module BIG_ASM (
  input  [31:0] DATA_INPUT,
  input  [31:0] MEMORY_IN,
  input  CLK,
  input  CLR,
  output [23:0] DIR_INPUT,
  output [31:0] MEMORY_OUT,
  output [23:0] DIR_MEMORY,
  output Write_OUTPUT,
  output [6:0] ASCII,
  output Write_ASCII,
  output END
);

  wire a____b, Check_i, Default_j, demultiplexer_3_out0, demultiplexer_3_out1, End_Print, END_t, First_j,
       First_j_1, First_j_2, Go_to_Idle, i____A_length, Idle, Index, Inf_End, j____B_length, L__A_Length,
       L__B_Length, L__elem_B, L__i, L__i_1, L__j, L__j_2, L__j_3, not_1_out, or_1_out, or_5_out, or_6_out,
       or_7_out, or_9_out, Print, Print_Space, Start, Stay_Idle, W_ASCII, Wait_4_q;
  wire [6:0] ASCII_t;
  wire [23:0] Def_j, i, j;
  wire [31:0] A_length, B_length, bit_extender_1_out, elem_a, elem_b, Input___Def, j_index;

  or or_1 (or_1_out, Go_to_Idle, Stay_Idle);
  D_Flip_Flop #(.trigger("falling")) u_Idle (.clk(CLK), .D(or_1_out), .Q(Idle), .preset(CLR));  // open: Qn, en, reset
  Demultiplexer #(.enable("false")) demultiplexer_1 (.out0(Stay_Idle), .out1(L__A_Length), .in(Idle), .sel(Start));
  and and_1 (Start, CLK, ~CLR);  // AND_Gate
  Register #(.width(32), .trigger("falling")) u_A_Length (
    .D(DATA_INPUT), .en(L__A_Length), .Q(A_length), .clk(CLK), .clr(CLR));
  Register #(.width(32), .trigger("falling")) u_elem_A (.D(DATA_INPUT), .en(Index), .Q(elem_a), .clk(CLK), .clr(CLR));
  D_Flip_Flop #(.trigger("falling")) Load_A_lenght (
    .clk(CLK), .D(L__A_Length), .Q(Default_j), .reset(CLR));  // open: Qn, preset, en
  Register #(.width(32), .trigger("falling")) u_B_Length (
    .D(Input___Def), .en(L__B_Length), .Q(B_length), .clk(CLK), .clr(CLR));
  Register #(.width(32), .trigger("falling")) u_elem_B (
    .D(DATA_INPUT), .en(L__elem_B), .Q(elem_b), .clk(CLK), .clr(CLR));
  D_Flip_Flop #(.trigger("falling")) Wait (
    .clk(CLK), .D(Default_j), .Q(First_j_1), .reset(CLR));  // open: Qn, preset, en
  assign bit_extender_1_out = {{8{1'b0}}, Def_j};  // Bit_Extender bit_extender_1
  Adder #(.width(32)) adder_1 (.a(DATA_INPUT), .b(bit_extender_1_out), .out(Input___Def));  // open: cin, cout
  or or_2 (L__j, L__i_1, L__j_2, L__j_3);
  or or_3 (L__i, L__i_1, First_j_2);
  Counter #(.width(24), .max('hffffff), .trigger("falling")) u_i (
    .count(L__i), .Q(i), .clk(CLK), .clr(CLR));  // open: load, D, carry
  D_Flip_Flop #(.trigger("falling")) Wait_2 (
    .clk(CLK), .D(First_j_1), .Q(L__B_Length), .reset(CLR));  // open: Qn, preset, en
  Register #(.width(24), .trigger("falling")) u_Default_j (
    .D(j_index[23:0]), .en(Default_j), .Q(Def_j), .clk(CLK), .clr(CLR));
  D_Flip_Flop #(.trigger("falling")) Load_B_length (
    .clk(CLK), .D(L__B_Length), .Q(L__i_1), .reset(CLR));  // open: Qn, preset, en
  Adder #(.width(32)) adder_2 (.a(DATA_INPUT), .b(32'h1), .out(j_index));  // open: cin, cout
  Comparator #(.width(32)) comparator_1 (.a(elem_a), .b(elem_b), .eq(a____b));  // open: gt, lt
  Comparator #(.width(24)) comparator_2 (.a(B_length[23:0]), .b(j), .eq(j____B_length));  // open: gt, lt
  Comparator #(.width(24)) comparator_3 (.a(A_length[23:0]), .b(i), .eq(i____A_length));  // open: gt, lt
  or or_4 (First_j, First_j_1, First_j_2);
  Counter #(.width(24), .max('hffffff), .trigger("falling")) u_j (
    .load(First_j), .D(Def_j), .count(L__j), .Q(j), .clk(CLK), .clr(CLR));  // open: carry
  or or_5 (or_5_out, L__i_1, L__j_3);
  D_Flip_Flop #(.trigger("falling")) While (.clk(CLK), .D(or_5_out), .Q(Index), .reset(CLR));  // open: Qn, preset, en
  Multiplexer #(.width(24), .enable("false")) multiplexer_1 (.in0(j), .in1(i), .out(DIR_INPUT), .sel(Index));
  Multiplexer #(.width(7), .enable("false")) multiplexer_2 (
    .in0(ASCII_t), .in1(7'b0100000), .out(ASCII), .sel(Print_Space));
  D_Flip_Flop #(.trigger("falling")) Wait_3 (
    .clk(CLK), .D(or_6_out), .Q(L__elem_B), .reset(CLR));  // open: Qn, preset, en
  or or_6 (or_6_out, Index, L__j_2);
  Demultiplexer #(.enable("false")) demultiplexer_2 (
    .out0(L__j_2), .out1(Print), .in(demultiplexer_3_out0), .sel(j____B_length));
  or or_7 (or_7_out, END_t, Inf_End);
  D_Flip_Flop #(.trigger("falling")) Wait_4 (
    .clk(CLK), .D(L__elem_B), .Q(Wait_4_q), .reset(CLR));  // open: Qn, preset, en
  Demultiplexer #(.enable("false")) demultiplexer_3 (
    .out0(demultiplexer_3_out0), .out1(demultiplexer_3_out1), .in(Wait_4_q), .sel(a____b));
  Demultiplexer #(.enable("false")) demultiplexer_4 (.out0(Inf_End), .out1(Go_to_Idle), .in(END), .sel(not_1_out));
  D_Flip_Flop #(.trigger("falling")) d_ff_1 (.clk(CLK), .D(or_7_out), .Q(END), .reset(CLR));  // open: Qn, preset, en
  not not_1 (not_1_out, Start);
  or or_8 (Write_ASCII, W_ASCII, Print_Space);
  D_Flip_Flop #(.trigger("falling")) Wait_5 (
    .clk(CLK), .D(End_Print), .Q(Print_Space), .reset(CLR));  // open: Qn, preset, en
  D_Flip_Flop #(.trigger("falling")) Wait_6 (
    .clk(CLK), .D(Print_Space), .Q(Check_i), .reset(CLR));  // open: Qn, preset, en
  PRINT_DEC print_dec_1 (
    .num(elem_a), .start(Print), .CLK(CLK), .RST(CLR), .ASCII(ASCII_t), .Write_ASCII(W_ASCII), .END(End_Print));
  or or_9 (or_9_out, demultiplexer_3_out1, Check_i);
  Demultiplexer #(.enable("false")) demultiplexer_5 (
    .out0(First_j_2), .out1(END_t), .in(or_9_out), .sel(i____A_length));
  D_Flip_Flop #(.trigger("falling")) Wait_7 (
    .clk(CLK), .D(First_j_2), .Q(L__j_3), .reset(CLR));  // open: Qn, preset, en

  // Other names for the same wires on the sheet: Input[31:0] = DATA_INPUT; L__elem_A = Index; L__i_2 = First_j_2;
  //   L__j_1 = L__i_1; Nxt_i = L__j_3; Nxt_j = L__j_2; True_End = END

  // Notes on the sheet:
  //   a != b
  //   a == b
endmodule

module PRINT_UDEC (
  input  [31:0] num,
  input  start,
  input  CLK,
  input  RST,
  output [6:0] ASCII,
  output Write_ASCII,
  output \end 
);

  wire _0_c, _0_n, demultiplexer_1_out0, demultiplexer_2_out0, demultiplexer_2_out1, demultiplexer_3_out0,
       demultiplexer_3_out1, IDLE_2_q, IDLE_3_q, IDLE_4_q, IDLE_q, Lc, Lc_0, Ln, Ln_0, or_1_out;
  wire [23:0] bit_extender_1_out;
  wire [31:0] c, c___1, c___1_t, divider_1_rem, memory_1_data_out, multiplexer_1_out, multiplexer_2_out,
       multiplexer_3_out, n, n___10, n___10___48;

  Multiplexer #(.width(32), .enable("false")) multiplexer_1 (
    .in0(num), .in1(n___10), .out(multiplexer_1_out), .sel(Lc_0));
  Divider #(.width(32)) divider_1 (.a(n), .b(32'ha), .out(n___10), .rem(divider_1_rem));  // open: upper
  Adder #(.width(32)) adder_1 (.a(divider_1_rem), .b(32'h30), .out(n___10___48));  // open: cin, cout
  or or_1 (or_1_out, demultiplexer_1_out0, \end );
  Register #(.width(32)) u_n (.D(multiplexer_1_out), .en(Ln), .Q(n), .clk(CLK), .clr(RST));
  D_Flip_Flop IDLE (.clk(CLK), .D(or_1_out), .Q(IDLE_q), .preset(RST));  // open: Qn, en, reset
  Demultiplexer #(.enable("false")) demultiplexer_1 (
    .out0(demultiplexer_1_out0), .out1(Ln_0), .in(IDLE_q), .sel(start));
  or or_2 (Write_ASCII, demultiplexer_3_out0, demultiplexer_2_out1);
  Multiplexer #(.width(32), .enable("false")) multiplexer_2 (
    .in0(c___1), .in1(c___1_t), .out(multiplexer_2_out), .sel(Write_ASCII));
  Adder #(.width(32)) adder_2 (.a(c), .b(32'h1), .out(c___1));  // open: cin, cout
  Subtractor #(.width(32)) subtractor_1 (.a(c), .b(32'h1), .out(c___1_t));  // open: bin, bout
  D_Flip_Flop IDLE_2 (.clk(CLK), .D(Ln_0), .Q(IDLE_2_q), .reset(RST));  // open: Qn, preset, en
  Register #(.width(32)) u_c (.D(multiplexer_2_out), .en(Lc), .Q(c), .clk(CLK), .clr(RST));
  or or_3 (Lc_0, IDLE_2_q, demultiplexer_3_out1);
  Multiplexer #(.width(32), .enable("false")) multiplexer_3 (
    .in0(c), .in1(c___1_t), .out(multiplexer_3_out), .sel(Write_ASCII));
  Comparator #(.width(32), .mode("unsigned")) comparator_1 (.a({32{1'b0}}), .b(n), .lt(_0_n));  // open: gt, eq
  Comparator #(.width(32), .mode("unsigned")) comparator_2 (.a({32{1'b0}}), .b(c), .lt(_0_c));  // open: gt, eq
  D_Flip_Flop IDLE_3 (.clk(CLK), .D(Write_ASCII), .Q(IDLE_3_q), .reset(RST));  // open: Qn, preset, en
  Demultiplexer #(.enable("false")) demultiplexer_2 (
    .out0(demultiplexer_2_out0), .out1(demultiplexer_2_out1), .in(IDLE_3_q), .sel(_0_c));
  Bit_Extender #(.in_width(32), .out_width(24)) bit_extender_1 (.in(multiplexer_3_out), .out(bit_extender_1_out));
  D_Flip_Flop IDLE_4 (.clk(CLK), .D(Lc_0), .Q(IDLE_4_q), .reset(RST));  // open: Qn, preset, en
  or or_4 (Lc, Lc_0, Write_ASCII);
  or or_5 (Ln, Ln_0, Lc_0);
  Demultiplexer #(.enable("false")) demultiplexer_3 (
    .out0(demultiplexer_3_out0), .out1(demultiplexer_3_out1), .in(IDLE_4_q), .sel(_0_n));
  D_Flip_Flop IDLE_5 (.clk(CLK), .D(demultiplexer_2_out0), .Q(\end ), .reset(RST));  // open: Qn, preset, en
  MEMORY memory_1 (
    .DIR(bit_extender_1_out), .DATA_IN(n___10___48), .WRITE(Lc_0), .CLK(CLK), .CLR(RST),
    .DATA_OUT(memory_1_data_out));
  Bit_Extender #(.in_width(32), .out_width(7)) bit_extender_2 (.in(memory_1_data_out), .out(ASCII));

  // Other names for the same wires on the sheet: Lc_1 = Write_ASCII; Sc = Write_ASCII; Ln_1 = Lc_0; Sn = Lc_0;
  //   Write = Lc_0
endmodule

module PRINT_DEC (
  input  [31:0] num,
  input  start,
  input  CLK,
  input  RST,
  output [6:0] ASCII,
  output Write_ASCII,
  output END
);

  wire demultiplexer_1_out0, demultiplexer_1_out1, demultiplexer_2_out0, demultiplexer_3_out0, end_t,
       IDLE_3_q, IDLE_q, or_1_out, or_2_out, or_3_out, S_ASCII, startUDEC, Write_ASCII_1;
  wire [6:0] ASCII_t;
  wire [31:0] multiplexer_1_out, negator_1_out;

  or or_1 (or_1_out, demultiplexer_1_out0, END);
  Negator #(.width(32)) negator_1 (.in(num), .out(negator_1_out));
  D_Flip_Flop IDLE (.clk(CLK), .D(or_1_out), .Q(IDLE_q), .preset(RST));  // open: Qn, en, reset
  Demultiplexer #(.enable("false")) demultiplexer_1 (
    .out0(demultiplexer_1_out0), .out1(demultiplexer_1_out1), .in(IDLE_q), .sel(start));
  Multiplexer #(.width(32), .enable("false")) multiplexer_1 (
    .in0(num), .in1(negator_1_out), .out(multiplexer_1_out), .sel(num[31]));
  Demultiplexer #(.enable("false")) demultiplexer_2 (
    .out0(demultiplexer_2_out0), .out1(S_ASCII), .in(demultiplexer_1_out1), .sel(num[31]));
  or or_2 (or_2_out, demultiplexer_2_out0, S_ASCII);
  D_Flip_Flop IDLE_2 (.clk(CLK), .D(or_2_out), .Q(startUDEC), .reset(RST));  // open: Qn, preset, en
  PRINT_UDEC print_udec_1 (
    .num(multiplexer_1_out), .start(startUDEC), .CLK(CLK), .RST(RST), .ASCII(ASCII_t),
    .Write_ASCII(Write_ASCII_1), .\end (end_t));
  D_Flip_Flop IDLE_3 (.clk(CLK), .D(or_3_out), .Q(IDLE_3_q), .reset(RST));  // open: Qn, preset, en
  or or_3 (or_3_out, startUDEC, demultiplexer_3_out0);
  Demultiplexer #(.enable("false")) demultiplexer_3 (
    .out0(demultiplexer_3_out0), .out1(END), .in(IDLE_3_q), .sel(end_t));
  Multiplexer #(.width(7), .enable("false")) multiplexer_2 (
    .in0(ASCII_t), .in1(7'b0101101), .out(ASCII), .sel(S_ASCII));
  or or_4 (Write_ASCII, S_ASCII, Write_ASCII_1);

  // Other names for the same wires on the sheet: sign = num[31]; Write_ASCII_0 = S_ASCII
endmodule

module TEST_PRINT (
  input  [31:0] in_1,
  output out_2
);

  wire button_1_out, button_2_out, CLK, CLR, d_ff_1_q, Write_ASCII;
  wire [6:0] ASCII;

  Button button_1 (.out(button_1_out));
  Clock clock_1 (.out(CLK));
  D_Flip_Flop d_ff_1 (.clk(CLK), .D(1'b1), .Q(d_ff_1_q), .reset(button_1_out));  // open: Qn, preset, en
  D_Flip_Flop d_ff_2 (.clk(CLK), .D(d_ff_1_q), .Qn(CLR), .reset(button_1_out));  // open: Q, preset, en
  Button button_2 (.out(button_2_out));
  PRINT_UDEC print_udec_1 ();  // open: num, start, CLK, RST, ASCII, Write_ASCII, end
  PRINT_DEC print_dec_1 (
    .num(in_1), .start(button_2_out), .CLK(CLK), .RST(CLR), .ASCII(ASCII), .Write_ASCII(Write_ASCII),
    .END(out_2));
  TTY #(.rows(32), .cols(60)) tty_1 (.data(ASCII), .clk(CLK), .we(Write_ASCII), .clr(CLR));
endmodule
